// Logisim project Ctl_Data_Processing.circ as structural Verilog: 1 circuit, main circuit Data_Processing
module Data_Processing (
  input  Enable,
  input  [15:0] Instruction,
  output [2:0] Rd,
  output [2:0] Rn,
  output [2:0] Rm,
  output [3:0] ALU_Opcode,
  output [3:0] Flags_Update_Mask
);

  wire [2:0] Rd_t;
  wire [3:0] Flag;

  Demultiplexer #(.select(4), .width(3)) demultiplexer_1 (
    .out0(Rd_t), .out1(Rd_t), .out2(Rd_t), .out3(Rd_t), .out4(Rd_t), .out5(Rd_t), .out6(Rd_t), .out7(Rd_t),
    .out8(Rd_t), .out9(Rd_t), .out10(Rd_t), .out11(Rd_t), .out12(Rd_t), .out13(Rd_t), .out14(Rd_t),
    .out15(Rd_t), .in(Instruction[2:0]), .sel(Instruction[9:6]));
  Demultiplexer #(.select(4), .width(3)) demultiplexer_2 (
    .out0(Rd_t), .out1(Rd_t), .out2(Rd_t), .out3(Rd_t), .out4(Rd_t), .out5(Rd_t), .out6(Rd_t), .out7(Rd_t),
    .out8(Rd_t), .out9(Rd_t), .out10(Rd_t), .out11(Rd_t), .out12(Rd_t), .out13(Rd_t), .out14(Rd_t),
    .out15(Rd_t), .in(Instruction[5:3]), .sel(Instruction[9:6]));
  Multiplexer #(.select(4), .width(4)) multiplexer_1 (
    .in0(4'b0011), .in1(4'b0011), .in2(4'b1011), .in3(4'b1011), .in4(4'b1011), .in5(4'b1111), .in6(4'b0111),
    .in7(4'b1011), .in8(4'b1111), .in9(4'b0111), .in10(4'b1111), .in11(4'b1111), .in12(4'b0011),
    .in13(4'b0011), .in14(4'b0011), .in15(4'b0011), .out(Flag), .sel(Instruction[9:6]));
  Multiplexer #(.width(3)) multiplexer_2 (.in0(3'b000), .in1(Rd_t), .out(Rd), .sel(Enable));
  Multiplexer #(.width(3)) multiplexer_3 (.in0(3'b000), .in1(Rd_t), .out(Rn), .sel(Enable));
  Multiplexer #(.width(3)) multiplexer_4 (.in0(3'b000), .in1(Rd_t), .out(Rm), .sel(Enable));
  Multiplexer #(.width(4)) multiplexer_5 (.in0(4'b0000), .in1(Instruction[9:6]), .out(ALU_Opcode), .sel(Enable));
  Multiplexer #(.width(4)) multiplexer_6 (.in0(4'b0000), .in1(Flag), .out(Flags_Update_Mask), .sel(Enable));

  // Other names for the same wires on the sheet: En = Enable; OperandDroite[2:0] = Instruction[2:0];
  //   OperandGauche[2:0] = Instruction[5:3]; ALU[3:0] = Instruction[9:6]; Rdm[2:0] = Rd_t; Rdn[2:0] = Rd_t;
  //   Rm_t[2:0] = Rd_t; Rn_t[2:0] = Rd_t
endmodule
