// Logisim project Ctl_Load_Store.circ as structural Verilog: 1 circuit, main circuit Load_Store
module Load_Store (
  input  Enable,
  input  Clk,
  input  Reset,
  input  [31:0] Stack_Pointer,
  input  [15:0] Instruction,
  output Store,
  output Load,
  output PC_Hold,
  output [2:0] Rmd,
  output [31:0] RAM_Addr
);

  wire and_1_out, Hold, Load_t, not_1_out, not_2_out;
  wire [31:0] bit_extender_1_out, CalcRam, multiplier_1_out, RamAddr;

  assign bit_extender_1_out = {{24{1'b0}}, Instruction[7:0]};  // Bit_Extender bit_extender_1
  Multiplier #(.width(32)) multiplier_1 (.a(bit_extender_1_out), .b(32'h4), .out(multiplier_1_out));  // open: cin, cout
  and and_1 (and_1_out, Instruction[11], ~Load_t);  // AND_Gate
  D_Flip_Flop d_ff_1 (.D(and_1_out), .clk(Clk), .Q(Load_t), .Qn(Hold), .reset(Reset));  // open: preset
  Register #(.width(32)) register_1 (.D(CalcRam), .en(not_1_out), .clk(Clk), .Q(RamAddr), .clr(Reset));
  not not_1 (not_1_out, Instruction[11]);
  Adder #(.width(32)) adder_1 (.a(multiplier_1_out), .b(Stack_Pointer), .out(CalcRam));  // open: cin, cout
  not not_2 (not_2_out, Instruction[11]);
  Multiplexer #(.width(3)) multiplexer_1 (.in0(3'b000), .in1(Instruction[10:8]), .out(Rmd), .sel(Enable));
  and and_2 (Store, not_2_out, Enable);
  and and_3 (Load, Enable, Instruction[11], Load_t);
  and and_4 (PC_Hold, Enable, Instruction[11], Hold);
  Multiplexer #(.width(32)) multiplexer_2 (.in0({32{1'b0}}), .in1(RamAddr), .out(RAM_Addr), .sel(Enable));

  // Other names for the same wires on the sheet: Clock = Clk; Imm8[7:0] = Instruction[7:0];
  //   Rdm[2:0] = Instruction[10:8]; IsLoad = Instruction[11]; Sp[31:0] = Stack_Pointer

  // Notes on the sheet:
  //   Delay load and hold PC for 1 cycle for the RAM to send out requested data 
endmodule
