// Logisim project Ctl_Shift_Add_Sub_Mov.circ as structural Verilog: 1 circuit, main circuit Shift_Add_Sub_Mov
module Shift_Add_Sub_Mov (
  input  Enable,
  input  [3:0] in_2,
  input  [3:0] in_3,
  input  [3:0] in_4,
  input  [15:0] Instruction,
  input  [3:0] in_6,
  input  [3:0] in_7,
  input  [3:0] in_8,
  input  [3:0] in_9,
  input  [3:0] in_10,
  input  [3:0] in_11,
  input  [3:0] in_12,
  output [3:0] Flags_Update_Mask,
  output Carry,
  output Imm32_Enable,
  output [2:0] Rm,
  output [2:0] Rn,
  output [2:0] Rd,
  output [4:0] Imm5,
  output [31:0] Imm32,
  output [3:0] ALU_Opcode
);

  wire and_4_out, and_5_out, and_6_out, and_7_out, and_9_out, is_ADD, is_ADD_or_SUB, is_ASRS, is_CMP, is_LS,
       is_LSLS, is_LSRS, is_MOVS, is_Shift, is_SUB, not_1_out, not_2_out, not_3_out, not_4_out, not_5_out,
       not_6_out, not_7_out, not_8_out, not_9_out, not_10_out, or_1_out;
  wire [2:0] multiplexer_13_out, multiplexer_15_out;
  wire [3:0] multiplexer_1_out, multiplexer_2_out, multiplexer_3_out, multiplexer_4_out, multiplexer_5_out,
       multiplexer_6_out, multiplexer_7_out, multiplexer_19_out;
  wire [31:0] multiplexer_18_out;

  not not_1 (not_1_out, Instruction[12]);
  not not_2 (not_2_out, Instruction[11]);
  not not_3 (not_3_out, Instruction[13]);
  not not_4 (not_4_out, Instruction[11]);
  and and_1 (is_ADD_or_SUB, Instruction[13], Instruction[12]);
  not not_5 (not_5_out, Instruction[13]);
  not not_6 (not_6_out, Instruction[13]);
  not not_7 (not_7_out, Instruction[12]);
  not not_8 (not_8_out, Instruction[12]);
  and and_2 (is_LS, not_1_out, not_2_out);
  and and_3 (is_ASRS, not_3_out, and_4_out);
  and and_4 (and_4_out, Instruction[12], not_4_out);
  and and_5 (and_5_out, not_5_out, Instruction[12]);
  and and_6 (and_6_out, not_7_out, Instruction[11]);
  and and_7 (and_7_out, not_8_out, Instruction[11]);
  not not_9 (not_9_out, Instruction[13]);
  and and_8 (is_SUB, is_ADD_or_SUB, or_1_out);
  or or_1 (or_1_out, Instruction[9], Instruction[11]);
  or or_2 (is_ADD, is_ADD_or_SUB, and_9_out);
  and and_9 (and_9_out, and_5_out, Instruction[11]);
  and and_10 (is_MOVS, not_6_out, and_6_out);
  and and_11 (is_CMP, Instruction[13], and_7_out);
  and and_12 (is_LSLS, not_9_out, is_LS);
  and and_13 (is_LSRS, Instruction[13], is_LS);
  and and_14 (is_Shift, is_LS, is_ASRS);
  Multiplexer #(.width(4)) multiplexer_1 (.in0(in_6), .in1(in_7), .out(multiplexer_1_out), .sel(is_MOVS));
  Multiplexer #(.width(4)) multiplexer_2 (.in0(multiplexer_1_out), .in1(in_8), .out(multiplexer_2_out), .sel(is_ADD));
  Multiplexer #(.width(4)) multiplexer_3 (.in0(multiplexer_2_out), .in1(in_9), .out(multiplexer_3_out), .sel(is_SUB));
  Multiplexer #(.width(4)) multiplexer_4 (.in0(in_2), .in1(in_3), .out(multiplexer_4_out), .sel(is_Shift));
  Multiplexer #(.width(4)) multiplexer_5 (.in0(multiplexer_3_out), .in1(in_10), .out(multiplexer_5_out), .sel(is_ASRS));
  Multiplexer #(.width(4)) multiplexer_6 (.in0(multiplexer_4_out), .in1(in_4), .out(multiplexer_6_out), .sel(is_MOVS));
  not not_10 (not_10_out, is_Shift);
  Multiplexer #(.width(4)) multiplexer_7 (.in0(multiplexer_5_out), .in1(in_11), .out(multiplexer_7_out), .sel(is_LSRS));
  Multiplexer #(.width(4)) multiplexer_8 (
    .in0(4'b0000), .in1(multiplexer_6_out), .out(Flags_Update_Mask), .sel(Enable));
  Multiplexer multiplexer_9 (.in0(1'b0), .in1(is_SUB), .out(Carry), .sel(Enable));
  Multiplexer multiplexer_10 (.in0(1'b0), .in1(not_10_out), .out(Imm32_Enable), .sel(Enable));
  Multiplexer #(.width(3)) multiplexer_11 (.in0(3'b000), .in1(Instruction[8:6]), .out(Rm), .sel(Enable));
  Multiplexer #(.width(3)) multiplexer_12 (.in0(3'b000), .in1(multiplexer_13_out), .out(Rn), .sel(Enable));
  Multiplexer #(.width(3)) multiplexer_13 (
    .in0(Instruction[10:8]), .in1(Instruction[5:3]), .out(multiplexer_13_out), .sel(Instruction[11]));
  Multiplexer #(.width(3)) multiplexer_14 (.in0(3'b000), .in1(multiplexer_15_out), .out(Rd), .sel(Enable));
  Multiplexer #(.width(3)) multiplexer_15 (
    .in0(Instruction[2:0]), .in1(Instruction[10:8]), .out(multiplexer_15_out), .sel(Instruction[11]));
  Multiplexer #(.width(5)) multiplexer_16 (.in0({5{1'b0}}), .in1(Instruction[10:6]), .out(Imm5), .sel(Enable));
  Multiplexer #(.width(32)) multiplexer_17 (.in0({32{1'b0}}), .in1(multiplexer_18_out), .out(Imm32), .sel(Enable));
  Multiplexer #(.width(32)) multiplexer_18 (
    .in0({Instruction[8:6], {29{1'b0}}}), .in1({Instruction[7:0], {24{1'b0}}}), .out(multiplexer_18_out),
    .sel(Instruction[11]));
  Multiplexer #(.width(4)) multiplexer_19 (
    .in0(multiplexer_7_out), .in1(in_12), .out(multiplexer_19_out), .sel(is_LSLS));
  Multiplexer #(.width(4)) multiplexer_20 (.in0(4'b0000), .in1(multiplexer_19_out), .out(ALU_Opcode), .sel(Enable));

  // Other names for the same wires on the sheet: bits_10_0[10:0] = Instruction[10:0]; imm5_t[4:0] = Instruction[10:6];
  //   Rdn[2:0] = Instruction[10:8]; Rm_imm3[2:0] = Instruction[8:6]; imm8[7:0] = Instruction[7:0];
  //   Rd_bits_2_0[2:0] = Instruction[2:0]; Rn_t[2:0] = Instruction[5:3]; is_b13 = Instruction[11];
  //   Operande[2:0] = Instruction[13:11]; is_b12 = Instruction[12]; is_b11 = Instruction[13]

  // Notes on the sheet:
  //   in_11: initial=0x11
  //   in_12: initial=0x10
  //   Note: ALU uses Rn register for shifts. Use Rn instead of Rm for shifts (immediate) here too
  //   Note 3: Imm32_Enable forces the use of the immediate for Rm register
  //   Note 2: MOV uses RSB ALU opcode with Imm8 reversed so that it is copied to output register
  //   Pull output low on Enable = 0
  //   only ADD and SUB use Rm
  //   Enable carry for SUB since it is reversed in ALU
  //   ALU will use Imm32 instead of Rm
endmodule
